// Logisim project cpu.circ as structural Verilog: 11 circuits, main circuit CPU
module CPU (
  input  [31:0] Instruction,
  input  CLK,
  output [31:0] s0,
  output [31:0] s1,
  output [31:0] t0,
  output [31:0] t1,
  output [31:0] a0,
  output [31:0] ra,
  output [31:0] sp,
  output [31:0] PC
);

  wire Asel, BrUN, Bsel, jump, PCsel, SelWR, WE;
  wire [1:0] SelWB;
  wire [2:0] Immsele, ImmSelec;
  wire [3:0] ALUselec;
  wire [6:0] undriven;
  wire [31:0] A, B, Imm, main_1_p5, multiplexer_1_out, PC___4, R1, R2, Res, undriven_2, W;

  // Incrementer incrementer_1: pin names not known; wires that end beside it: PC, PC___4
  Control_xd control_xd_1 (
    .in_1(Instruction), .jump(jump), .Imm_sle(ImmSelec), .Alu_se(ALUselec), .Asele(Asel), .Bsle(Bsel),
    .BrUn(BrUN), .MemRw(SelWR), .WE(WE), .Pcsele(PCsel), .WBselec(SelWB));
  Multiplexer #(.width(32), .enable("false")) multiplexer_1 (
    .in0(PC___4), .in1(Res), .out(multiplexer_1_out), .sel(PCsel));
  br_compaator br_compaator_1 (.in_3(Instruction[14:12]), .in_1(R2), .in_2(R1), .out_4(jump));
  // PC pc_1: pin names not known; wires that end beside it: multiplexer_1_out, CLK, PC
  RegFile regfile_1 (
    .Clk(CLK), .R1(R1), .R2(R2), .WE(WE), .W(W), .RD(Instruction[11:7]), .RS1(Instruction[19:15]),
    .RS2(Instruction[24:20]), .s0(s0), .s1(s1), .t0(t0), .t1(t1), .a0(a0), .ra(ra), .sp(sp));
  immediato_gene immediato_gene_1 (.in_1(Instruction), .in_2(Imm), .in_3(Immsele));
  Multiplexer #(.width(32), .enable("false")) multiplexer_2 (.in0(PC), .in1(R1), .out(A), .sel(Asel));
  Multiplexer #(.width(32), .enable("false")) multiplexer_3 (.in0(Imm), .in1(R2), .out(B), .sel(Bsel));
  br_compar br_compar_1 (.OPc(undriven), .f3(Instruction[14:12]), .f7(Instruction[31:25]), .Alusle(ALUselec));
  ALU alu_1 (.A(A), .B(B), .Out(Res));  // open: ALU_Op
  // memory_main main_1: pin names not known; wires that end beside it: Res, SelWR, R2, CLK, main_1_p5
  Multiplexer #(.select(2), .width(32), .enable("false")) multiplexer_4 (
    .in1(PC___4), .in2(Res), .in3(undriven_2), .out(W), .sel(SelWB));  // open: in0
  ld ld_1 (.in_1(main_1_p5), .f3(Instruction[14:12]), .ld(undriven_2));

  // Other names for the same wires on the sheet: fetch_addr[31:0] = PC; INST[31:0] = Instruction;
  //   Opcode[6:0] = Instruction[6:0]; RD[4:0] = Instruction[11:7]; f3[2:0] = Instruction[14:12];
  //   RS1[4:0] = Instruction[19:15]; RS2[4:0] = Instruction[24:20]; f7[6:0] = Instruction[31:25]

  // Notes on the sheet:
  //   NOTE
  //   Please do not modify/replace/move/change/delete/etc input and output pins
  //   These are debug/test outputs from your circuit
endmodule

module jump (
  input  [2:0] f3,
  input  [31:0] R1,
  input  [31:0] R2,
  input  in_4
);

  wire comparator_1_gt, comparator_2_eq, comparator_2_gt, multiplexer_1_out, multiplexer_2_out, not_1_out;

  Comparator #(.width(32), .mode("unsigned")) comparator_1 (.a(R1), .b(R2), .gt(comparator_1_gt));  // open: eq, lt
  Comparator #(.width(32)) comparator_2 (.a(R1), .b(R2), .gt(comparator_2_gt), .eq(comparator_2_eq));  // open: lt
  Multiplexer multiplexer_1 (
    .in0(comparator_1_gt), .in1(comparator_2_gt), .out(multiplexer_1_out), .sel(f3[1]));  // open: en
  Multiplexer multiplexer_2 (
    .in0(multiplexer_1_out), .in1(comparator_2_eq), .out(multiplexer_2_out), .sel(f3[2]));  // open: en
  not not_1 (not_1_out, multiplexer_2_out);
  Multiplexer multiplexer_3 (.in0(multiplexer_2_out), .in1(not_1_out), .out(in_4), .sel(f3[0]));  // open: en
  // Probe on in_4

  // Other names for the same wires on the sheet: f3_0 = f3[0]; f3_1 = f3[1]; f3_2 = f3[2]
endmodule

module select (
  input  in_1,
  input  in_2
);
endmodule

module T_select (
  input  [31:0] in_1,
  input  in_2
);


  // Other names for the same wires on the sheet: INST[31:0] = in_1; jump = in_2
endmodule

module RW_selc (
  input  in_1,
  output out_2
);

  Multiplexer multiplexer_1 (.in0(1'b1), .in1(1'b0), .out(out_2), .sel(in_1));  // open: en
endmodule

module immediato_gene (
  input  [31:0] in_1,
  input  [31:0] in_2,
  input  [2:0] in_3
);

  wire [31:0] bit_extender_1_out, bit_extender_2_out, bit_extender_3_out, bit_extender_4_out,
       bit_extender_5_out, shifter_1_out;

  assign bit_extender_1_out = {{20{in_1[31]}}, in_1[31:20]};  // Bit_Extender bit_extender_1
  assign bit_extender_2_out = {{12{in_1[31]}}, in_1[31:12]};  // Bit_Extender bit_extender_2
  assign bit_extender_3_out = {{20{in_1[31]}}, {in_1[31:25], in_1[11:7]}};  // Bit_Extender bit_extender_3
  assign bit_extender_4_out = {{11{in_1[31]}}, {in_1[31], in_1[19:12], in_1[20], in_1[30:21], 1'b0}};  // Bit_Extender bit_extender_4
  assign bit_extender_5_out = {{19{in_1[31]}}, {in_1[31], in_1[7], in_1[30:25], in_1[11:8], 1'b0}};  // Bit_Extender bit_extender_5
  Shifter #(.width(32)) shifter_1 (.in(bit_extender_2_out), .\dist (5'b01100), .out(shifter_1_out));
  Multiplexer #(.select(3), .width(32)) multiplexer_1 (
    .in0(bit_extender_1_out), .in1(bit_extender_3_out), .in2(bit_extender_5_out), .in3(shifter_1_out),
    .in4(bit_extender_4_out), .in5({32{1'b0}}), .in6({32{1'b0}}), .in7({32{1'b0}}), .out(in_2), .sel(in_3));  // open: en

  // Other names for the same wires on the sheet: INST[31:0] = in_1; Imm[31:0] = in_2; Immsele[2:0] = in_3
endmodule

module br_compar (
  input  [6:0] OPc,
  input  [2:0] f3,
  input  [6:0] f7,
  output [3:0] Alusle
);

  wire comparator_1_eq, comparator_2_eq, comparator_3_eq, comparator_4_eq, comparator_5_eq, comparator_6_eq,
       comparator_7_eq, comparator_8_eq, comparator_9_eq, comparator_10_eq, comparator_11_eq,
       comparator_12_eq, comparator_13_eq, comparator_14_eq, comparator_15_eq, comparator_16_eq,
       comparator_17_eq, comparator_18_eq, comparator_19_eq, comparator_20_eq, comparator_21_eq,
       comparator_22_eq, comparator_23_eq, comparator_24_eq, comparator_25_eq, comparator_26_eq,
       comparator_27_eq, comparator_28_eq, comparator_29_eq, comparator_30_eq, comparator_31_eq,
       comparator_32_eq, comparator_33_eq, comparator_34_eq, comparator_35_eq;
  wire [3:0] ALUs, I, R, Selec;
  wire [6:0] multiplexer_19_out, multiplexer_20_out, multiplexer_21_out, multiplexer_22_out,
       multiplexer_24_out, multiplexer_25_out, multiplexer_29_out, multiplexer_32_out, multiplexer_34_out,
       multiplexer_37_out, multiplexer_39_out, multiplexer_40_out;

  Comparator #(.width(3)) comparator_1 (.a(3'b000), .b(f3), .eq(comparator_1_eq));  // open: gt, lt
  Comparator #(.width(3)) comparator_2 (.a(3'b001), .b(f3), .eq(comparator_2_eq));  // open: gt, lt
  Comparator #(.width(3)) comparator_3 (.a(3'b010), .b(f3), .eq(comparator_3_eq));  // open: gt, lt
  Comparator #(.width(3)) comparator_4 (.a(3'b100), .b(f3), .eq(comparator_4_eq));  // open: gt, lt
  Comparator #(.width(3)) comparator_5 (.a(3'b101), .b(f3), .eq(comparator_5_eq));  // open: gt, lt
  Comparator #(.width(3)) comparator_6 (.a(3'b110), .b(f3), .eq(comparator_6_eq));  // open: gt, lt
  Comparator #(.width(3)) comparator_7 (.a(3'b111), .b(f3), .eq(comparator_7_eq));  // open: gt, lt
  Multiplexer #(.width(4)) multiplexer_1 (.in1(4'b0010), .out(I), .sel(comparator_1_eq));  // open: in0, en
  Multiplexer #(.width(4)) multiplexer_2 (.in1(4'b0000), .out(I), .sel(comparator_2_eq));  // open: in0, en
  Multiplexer #(.width(4)) multiplexer_3 (.in1(4'b0110), .out(I), .sel(comparator_3_eq));  // open: in0, en
  Multiplexer #(.width(4)) multiplexer_4 (.in1(4'b0101), .out(I), .sel(comparator_4_eq));  // open: in0, en
  Multiplexer #(.width(4)) multiplexer_5 (.in1(4'b0001), .out(I), .sel(comparator_5_eq));  // open: in0, en
  Multiplexer #(.width(4)) multiplexer_6 (.in1(4'b0100), .out(I), .sel(comparator_6_eq));  // open: in0, en
  Multiplexer #(.width(4)) multiplexer_7 (.in1(4'b0011), .out(I), .sel(comparator_7_eq));  // open: in0, en
  Multiplexer #(.select(4), .width(4)) multiplexer_8 (
    .in0(R), .in1(I), .in2(4'b0010), .in3(4'b0010), .in4(4'b0010), .in5(4'b1111), .in6(4'b0010),
    .in7(4'b0010), .in8(4'b0010), .out(Alusle), .sel(ALUs));  // open: in9, in10, in11, in12, in13, in14, in15, en
  Comparator #(.width(7)) comparator_8 (.a(OPc), .b(7'b0110011), .eq(comparator_8_eq));  // open: gt, lt
  Comparator #(.width(7)) comparator_9 (.a(OPc), .b(7'b0010011), .eq(comparator_9_eq));  // open: gt, lt
  Comparator #(.width(7)) comparator_10 (.a(OPc), .b(7'b0000011), .eq(comparator_10_eq));  // open: gt, lt
  Comparator #(.width(7)) comparator_11 (.a(OPc), .b(7'b0100011), .eq(comparator_11_eq));  // open: gt, lt
  Comparator #(.width(7)) comparator_12 (.a(OPc), .b(7'b1100011), .eq(comparator_12_eq));  // open: gt, lt
  Comparator #(.width(7)) comparator_13 (.a(OPc), .b(7'b0110111), .eq(comparator_13_eq));  // open: gt, lt
  Comparator #(.width(7)) comparator_14 (.a(OPc), .b(7'b0010111), .eq(comparator_14_eq));  // open: gt, lt
  Comparator #(.width(7)) comparator_15 (.a(OPc), .b(7'b1101111), .eq(comparator_15_eq));  // open: gt, lt
  Comparator #(.width(7)) comparator_16 (.a(OPc), .b(7'b1100111), .eq(comparator_16_eq));  // open: gt, lt
  Comparator #(.width(3)) comparator_17 (.a(3'b000), .b(f3), .eq(comparator_17_eq));  // open: gt, lt
  Comparator #(.width(3)) comparator_18 (.a(3'b001), .b(f3), .eq(comparator_18_eq));  // open: gt, lt
  Comparator #(.width(3)) comparator_19 (.a(3'b010), .b(f3), .eq(comparator_19_eq));  // open: gt, lt
  Comparator #(.width(3)) comparator_20 (.a(3'b100), .b(f3), .eq(comparator_20_eq));  // open: gt, lt
  Comparator #(.width(3)) comparator_21 (.a(3'b101), .b(f3), .eq(comparator_21_eq));  // open: gt, lt
  Comparator #(.width(3)) comparator_22 (.a(3'b110), .b(f3), .eq(comparator_22_eq));  // open: gt, lt
  Comparator #(.width(3)) comparator_23 (.a(3'b111), .b(f3), .eq(comparator_23_eq));  // open: gt, lt
  Multiplexer #(.select(4), .width(4)) multiplexer_9 (
    .in0(4'b0000), .in1(4'b0001), .in2(4'b0010), .in3(4'b0011), .in4(4'b0100), .in5(4'b0101), .in6(4'b0110),
    .in7(4'b0111), .in8(4'b1000), .out(ALUs), .sel(Selec));  // open: in9, in10, in11, in12, in13, in14, in15, en
  Multiplexer #(.width(4)) multiplexer_10 (.in1(4'b0000), .out(Selec), .sel(comparator_8_eq));  // open: in0, en
  Multiplexer #(.width(4)) multiplexer_11 (.in1(4'b0001), .out(Selec), .sel(comparator_9_eq));  // open: in0, en
  Multiplexer #(.width(4)) multiplexer_12 (.in1(4'b0010), .out(Selec), .sel(comparator_10_eq));  // open: in0, en
  Multiplexer #(.width(4)) multiplexer_13 (.in1(4'b0011), .out(Selec), .sel(comparator_11_eq));  // open: in0, en
  Multiplexer #(.width(4)) multiplexer_14 (.in1(4'b0100), .out(Selec), .sel(comparator_12_eq));  // open: in0, en
  Multiplexer #(.width(4)) multiplexer_15 (.in1(4'b0101), .out(Selec), .sel(comparator_13_eq));  // open: in0, en
  Multiplexer #(.width(4)) multiplexer_16 (.in1(4'b0110), .out(Selec), .sel(comparator_14_eq));  // open: in0, en
  Multiplexer #(.width(4)) multiplexer_17 (.in1(4'b0111), .out(Selec), .sel(comparator_15_eq));  // open: in0, en
  Multiplexer #(.width(4)) multiplexer_18 (.in1(4'b1000), .out(Selec), .sel(comparator_16_eq));  // open: in0, en
  Multiplexer #(.width(7)) multiplexer_19 (
    .in1(f7), .out(multiplexer_19_out), .sel(comparator_17_eq));  // open: in0, en
  Comparator #(.width(7)) comparator_24 (.a({7{1'b0}}), .b(multiplexer_19_out), .eq(comparator_24_eq));  // open: gt, lt
  Multiplexer #(.width(7)) multiplexer_20 (
    .in1(f7), .out(multiplexer_20_out), .sel(comparator_17_eq));  // open: in0, en
  Multiplexer #(.width(7)) multiplexer_21 (
    .in1(f7), .out(multiplexer_21_out), .sel(comparator_17_eq));  // open: in0, en
  Multiplexer #(.width(7)) multiplexer_22 (
    .in1(f7), .out(multiplexer_22_out), .sel(comparator_18_eq));  // open: in0, en
  Multiplexer #(.width(4)) multiplexer_23 (.in1(4'b0010), .out(R), .sel(comparator_24_eq));  // open: in0, en
  Comparator #(.width(7)) comparator_25 (
    .a(7'b0000001), .b(multiplexer_20_out), .eq(comparator_25_eq));  // open: gt, lt
  Comparator #(.width(7)) comparator_26 (
    .a(7'b0100000), .b(multiplexer_21_out), .eq(comparator_26_eq));  // open: gt, lt
  Comparator #(.width(7)) comparator_27 (.a({7{1'b0}}), .b(multiplexer_22_out), .eq(comparator_27_eq));  // open: gt, lt
  Multiplexer #(.width(7)) multiplexer_24 (
    .in1(f7), .out(multiplexer_24_out), .sel(comparator_18_eq));  // open: in0, en
  Multiplexer #(.width(7)) multiplexer_25 (
    .in1(f7), .out(multiplexer_25_out), .sel(comparator_19_eq));  // open: in0, en
  Multiplexer #(.width(4)) multiplexer_26 (.in1(4'b0111), .out(R), .sel(comparator_25_eq));  // open: in0, en
  Multiplexer #(.width(4)) multiplexer_27 (.in1(4'b1011), .out(R), .sel(comparator_26_eq));  // open: in0, en
  Multiplexer #(.width(4)) multiplexer_28 (.in1(4'b0000), .out(R), .sel(comparator_27_eq));  // open: in0, en
  Comparator #(.width(7)) comparator_28 (
    .a(7'b0000001), .b(multiplexer_24_out), .eq(comparator_28_eq));  // open: gt, lt
  Comparator #(.width(7)) comparator_29 (.a({7{1'b0}}), .b(multiplexer_25_out), .eq(comparator_29_eq));  // open: gt, lt
  Multiplexer #(.width(7)) multiplexer_29 (
    .in1(f7), .out(multiplexer_29_out), .sel(comparator_20_eq));  // open: in0, en
  Multiplexer #(.width(4)) multiplexer_30 (.in1(4'b1000), .out(R), .sel(comparator_28_eq));  // open: in0, en
  Multiplexer #(.width(4)) multiplexer_31 (.in1(4'b0110), .out(R), .sel(comparator_29_eq));  // open: in0, en
  Comparator #(.width(7)) comparator_30 (.a({7{1'b0}}), .b(multiplexer_29_out), .eq(comparator_30_eq));  // open: gt, lt
  Multiplexer #(.width(7)) multiplexer_32 (
    .in1(f7), .out(multiplexer_32_out), .sel(comparator_20_eq));  // open: in0, en
  Multiplexer #(.width(4)) multiplexer_33 (.in1(4'b0101), .out(R), .sel(comparator_30_eq));  // open: in0, en
  Comparator #(.width(7)) comparator_31 (
    .a(7'b0000001), .b(multiplexer_32_out), .eq(comparator_31_eq));  // open: gt, lt
  Multiplexer #(.width(7)) multiplexer_34 (
    .in1(f7), .out(multiplexer_34_out), .sel(comparator_21_eq));  // open: in0, en
  Multiplexer #(.width(4)) multiplexer_35 (.in1(4'b1001), .out(R), .sel(comparator_31_eq));  // open: in0, en
  Multiplexer #(.width(4)) multiplexer_36 (.in1(4'b0001), .out(R), .sel(comparator_32_eq));  // open: in0, en
  Comparator #(.width(7)) comparator_32 (.a({7{1'b0}}), .b(multiplexer_34_out), .eq(comparator_32_eq));  // open: gt, lt
  Multiplexer #(.width(7)) multiplexer_37 (
    .in1(f7), .out(multiplexer_37_out), .sel(comparator_22_eq));  // open: in0, en
  Multiplexer #(.width(4)) multiplexer_38 (.in1(4'b0100), .out(R), .sel(comparator_33_eq));  // open: in0, en
  Comparator #(.width(7)) comparator_33 (.a({7{1'b0}}), .b(multiplexer_37_out), .eq(comparator_33_eq));  // open: gt, lt
  Multiplexer #(.width(7)) multiplexer_39 (
    .in1(f7), .out(multiplexer_39_out), .sel(comparator_22_eq));  // open: in0, en
  Multiplexer #(.width(7)) multiplexer_40 (
    .in1(f7), .out(multiplexer_40_out), .sel(comparator_23_eq));  // open: in0, en
  Multiplexer #(.width(4)) multiplexer_41 (.in1(4'b1010), .out(R), .sel(comparator_34_eq));  // open: in0, en
  Comparator #(.width(7)) comparator_34 (
    .a(7'b0000001), .b(multiplexer_39_out), .eq(comparator_34_eq));  // open: gt, lt
  Multiplexer #(.width(4)) multiplexer_42 (.in1(4'b0011), .out(R), .sel(comparator_35_eq));  // open: in0, en
  Comparator #(.width(7)) comparator_35 (.a({7{1'b0}}), .b(multiplexer_40_out), .eq(comparator_35_eq));  // open: gt, lt

  // Other names for the same wires on the sheet: op[3:0] = Alusle; Opcode[6:0] = OPc
endmodule

module Control_xd (
  input  [31:0] in_1,
  input  jump,
  output [2:0] Imm_sle,
  output [3:0] Alu_se,
  output Asele,
  output Bsle,
  output BrUn,
  output MemRw,
  output WE,
  output Pcsele,
  output [1:0] WBselec
);

  wire BR, comparator_1_eq, comparator_2_eq, comparator_3_eq, comparator_4_eq, comparator_5_eq,
       comparator_6_eq, comparator_7_eq, comparator_8_eq, comparator_9_eq;
  wire [3:0] selec;

  Comparator #(.width(5)) comparator_1 (.a(in_1[6:2]), .b(5'b01100), .eq(comparator_1_eq));  // open: gt, lt
  Comparator #(.width(5)) comparator_2 (.a(in_1[6:2]), .b(5'b00100), .eq(comparator_2_eq));  // open: gt, lt
  Comparator #(.width(5)) comparator_3 (.a(in_1[6:2]), .b({5{1'b0}}), .eq(comparator_3_eq));  // open: gt, lt
  Comparator #(.width(5)) comparator_4 (.a(in_1[6:2]), .b(5'b01000), .eq(comparator_4_eq));  // open: gt, lt
  Comparator #(.width(5)) comparator_5 (.a(in_1[6:2]), .b(5'b11000), .eq(comparator_5_eq));  // open: gt, lt
  Comparator #(.width(5)) comparator_6 (.a(in_1[6:2]), .b(5'b01101), .eq(comparator_6_eq));  // open: gt, lt
  Comparator #(.width(5)) comparator_7 (.a(in_1[6:2]), .b(5'b00101), .eq(comparator_7_eq));  // open: gt, lt
  Comparator #(.width(5)) comparator_8 (.a(in_1[6:2]), .b(5'b11011), .eq(comparator_8_eq));  // open: gt, lt
  Comparator #(.width(5)) comparator_9 (.a(in_1[6:2]), .b(5'b11001), .eq(comparator_9_eq));  // open: gt, lt
  Multiplexer #(.width(4)) multiplexer_1 (.in1(4'b0000), .out(selec), .sel(comparator_1_eq));  // open: in0, en
  Multiplexer #(.width(4)) multiplexer_2 (.in1(4'b0001), .out(selec), .sel(comparator_2_eq));  // open: in0, en
  Multiplexer #(.width(4)) multiplexer_3 (.in1(4'b0010), .out(selec), .sel(comparator_3_eq));  // open: in0, en
  Multiplexer #(.width(4)) multiplexer_4 (.in1(4'b0011), .out(selec), .sel(comparator_4_eq));  // open: in0, en
  Multiplexer #(.width(4)) multiplexer_5 (.in1(4'b0100), .out(selec), .sel(comparator_5_eq));  // open: in0, en
  Multiplexer #(.width(4)) multiplexer_6 (.in1(4'b0101), .out(selec), .sel(comparator_6_eq));  // open: in0, en
  Multiplexer #(.width(4)) multiplexer_7 (.in1(4'b0110), .out(selec), .sel(comparator_7_eq));  // open: in0, en
  Multiplexer #(.width(4)) multiplexer_8 (.in1(4'b0111), .out(selec), .sel(comparator_8_eq));  // open: in0, en
  Multiplexer #(.width(4)) multiplexer_9 (.in1(4'b1000), .out(selec), .sel(comparator_9_eq));  // open: in0, en
  Multiplexer #(.enable("false")) multiplexer_10 (.in0(1'b0), .in1(1'b0), .out(BR), .sel(jump));
  Multiplexer #(.select(4)) multiplexer_11 (
    .in0(1'b1), .in1(1'b1), .in2(1'b1), .in3(1'b1), .in4(1'b0), .in5(1'b0), .in6(1'b0), .in7(1'b0),
    .in8(1'b1), .out(Asele), .sel(selec));  // open: in9, in10, in11, in12, in13, in14, in15, en
  Demultiplexer demultiplexer_1 ();  // open: out0, out1, in, sel, en
  Multiplexer #(.select(4)) multiplexer_12 (
    .in0(1'b1), .in1(1'b0), .in2(1'b0), .in3(1'b0), .in4(1'b0), .in5(1'b0), .in6(1'b0), .in7(1'b0),
    .in8(1'b0), .out(Bsle), .sel(selec));  // open: in9, in10, in11, in12, in13, in14, in15, en
  Multiplexer #(.select(4)) multiplexer_13 (
    .in0(1'b0), .in1(1'b0), .in2(1'b0), .in3(1'b0), .in4(1'b1), .in5(1'b0), .in6(1'b0), .in7(1'b0),
    .in8(1'b0), .out(BrUn), .sel(selec));  // open: in9, in10, in11, in12, in13, in14, in15, en
  Multiplexer #(.select(4)) multiplexer_14 (
    .in0(1'b0), .in1(1'b0), .in2(1'b0), .in3(1'b1), .in4(1'b0), .in5(1'b0), .in6(1'b0), .in7(1'b0),
    .in8(1'b0), .out(MemRw), .sel(selec));  // open: in9, in10, in11, in12, in13, in14, in15, en
  Multiplexer #(.select(4)) multiplexer_15 (
    .in0(1'b1), .in1(1'b1), .in2(1'b1), .in3(1'b0), .in4(1'b0), .in5(1'b1), .in6(1'b1), .in7(1'b1),
    .in8(1'b1), .out(WE), .sel(selec));  // open: in9, in10, in11, in12, in13, in14, in15, en
  Multiplexer #(.select(4)) multiplexer_16 (
    .in0(1'b1), .in1(1'b1), .in2(1'b1), .in3(1'b1), .in4(BR), .in5(1'b1), .in6(1'b1), .in7(1'b0), .in8(1'b0),
    .out(Pcsele), .sel(selec));  // open: in9, in10, in11, in12, in13, in14, in15, en
  Multiplexer #(.select(4), .width(2)) multiplexer_17 (
    .in0(2'b10), .in1(2'b10), .in2(2'b11), .in3(2'b00), .in4(2'b00), .in5(2'b10), .in6(2'b10), .in7(2'b01),
    .in8(2'b01), .out(WBselec), .sel(selec));  // open: in9, in10, in11, in12, in13, in14, in15, en
  Multiplexer #(.select(4), .width(3)) multiplexer_18 (
    .in0(3'b101), .in1(3'b000), .in2(3'b000), .in3(3'b001), .in4(3'b010), .in5(3'b011), .in6(3'b011),
    .in7(3'b100), .in8(3'b000), .out(Imm_sle), .sel(selec));  // open: in9, in10, in11, in12, in13, in14, in15, en
  Multiplexer #(.select(4), .width(4)) multiplexer_19 (
    .in0(4'b0000), .in1(4'b0001), .in2(4'b0010), .in3(4'b0011), .in4(4'b0100), .in5(4'b0101), .in6(4'b0110),
    .in7(4'b0111), .in8(4'b1000), .out(Alu_se), .sel(selec));  // open: in9, in10, in11, in12, in13, in14, in15, en
  Demultiplexer demultiplexer_2 ();  // open: out0, out1, in, sel, en
endmodule

module ld (
  input  [31:0] in_1,
  input  [31:0] ld,
  input  [2:0] f3
);

  wire [31:0] bit_extender_1_out, bit_extender_2_out;

  assign bit_extender_1_out = {{24{1'b0}}, in_1[7:0]};  // Bit_Extender bit_extender_1
  assign bit_extender_2_out = {{16{in_1[15]}}, in_1[15:0]};  // Bit_Extender bit_extender_2
  Multiplexer #(.select(3), .width(32)) multiplexer_1 (
    .in0(bit_extender_1_out), .in1(bit_extender_2_out), .in2(in_1), .out(ld), .sel(f3));  // open: in3, in4, in5, in6, in7, en
endmodule

module alu (
  input  [3:0] seleccc,
  input  [2:0] f3,
  input  [6:0] f7,
  input  in_4,
  input  in_5,
  output [3:0] alida
);

  wire cero, cinco, comparator_9_eq, comparator_10_eq, comparator_11_eq, comparator_12_eq, comparator_13_eq,
       comparator_14_eq, comparator_15_eq, comparator_16_eq, comparator_17_eq, comparator_18_eq,
       comparator_19_eq, comparator_20_eq, comparator_21_eq, comparator_22_eq, comparator_23_eq,
       comparator_24_eq, comparator_25_eq, comparator_26_eq, comparator_27_eq, cuatro, dos, seis, siete,
       tres, uno;
  wire [3:0] multiplexer_13_out, multiplexer_20_out;
  wire [6:0] multiplexer_1_out, multiplexer_2_out, multiplexer_3_out, multiplexer_4_out, multiplexer_5_out,
       multiplexer_6_out, multiplexer_7_out, multiplexer_8_out, multiplexer_9_out, multiplexer_10_out,
       multiplexer_11_out, multiplexer_12_out;

  Comparator #(.width(3)) comparator_1 (.a(f3), .b(3'b000), .eq(cero));  // open: gt, lt
  Comparator #(.width(3)) comparator_2 (.a(f3), .b(3'b001), .eq(uno));  // open: gt, lt
  Comparator #(.width(3)) comparator_3 (.a(f3), .b(3'b010), .eq(dos));  // open: gt, lt
  Comparator #(.width(3)) comparator_4 (.a(f3), .b(3'b011), .eq(tres));  // open: gt, lt
  Comparator #(.width(3)) comparator_5 (.a(f3), .b(3'b100), .eq(cuatro));  // open: gt, lt
  Comparator #(.width(3)) comparator_6 (.a(f3), .b(3'b101), .eq(cinco));  // open: gt, lt
  Comparator #(.width(3)) comparator_7 (.a(f3), .b(3'b110), .eq(seis));  // open: gt, lt
  Comparator #(.width(3)) comparator_8 (.a(f3), .b(3'b111), .eq(siete));  // open: gt, lt
  Multiplexer #(.width(7)) multiplexer_1 (.in1(f7), .out(multiplexer_1_out), .sel(cero));  // open: in0, en
  Multiplexer #(.width(7)) multiplexer_2 (.in1(f7), .out(multiplexer_2_out), .sel(cero));  // open: in0, en
  Multiplexer #(.width(7)) multiplexer_3 (.in1(f7), .out(multiplexer_3_out), .sel(cero));  // open: in0, en
  Multiplexer #(.width(7)) multiplexer_4 (.in1(f7), .out(multiplexer_4_out), .sel(uno));  // open: in0, en
  Multiplexer #(.width(7)) multiplexer_5 (.in1(f7), .out(multiplexer_5_out), .sel(uno));  // open: in0, en
  Multiplexer #(.width(7)) multiplexer_6 (.in1(f7), .out(multiplexer_6_out), .sel(dos));  // open: in0, en
  Multiplexer #(.width(7)) multiplexer_7 (.in1(f7), .out(multiplexer_7_out), .sel(cuatro));  // open: in0, en
  Multiplexer #(.width(7)) multiplexer_8 (.in1(f7), .out(multiplexer_8_out), .sel(cuatro));  // open: in0, en
  Multiplexer #(.width(7)) multiplexer_9 (.in1(f7), .out(multiplexer_9_out), .sel(cinco));  // open: in0, en
  Multiplexer #(.width(7)) multiplexer_10 (.in1(f7), .out(multiplexer_10_out), .sel(seis));  // open: in0, en
  Multiplexer #(.width(7)) multiplexer_11 (.in1(f7), .out(multiplexer_11_out), .sel(seis));  // open: in0, en
  Multiplexer #(.width(7)) multiplexer_12 (.in1(f7), .out(multiplexer_12_out), .sel(siete));  // open: in0, en
  Comparator #(.width(3)) comparator_9 (.a(f3), .b(3'b000), .eq(comparator_9_eq));  // open: gt, lt
  Comparator #(.width(3)) comparator_10 (.a(f3), .b(3'b001), .eq(comparator_10_eq));  // open: gt, lt
  Comparator #(.width(3)) comparator_11 (.a(f3), .b(3'b010), .eq(comparator_11_eq));  // open: gt, lt
  Comparator #(.width(3)) comparator_12 (.a(f3), .b(3'b100), .eq(comparator_12_eq));  // open: gt, lt
  Comparator #(.width(3)) comparator_13 (.a(f3), .b(3'b101), .eq(comparator_13_eq));  // open: gt, lt
  Comparator #(.width(3)) comparator_14 (.a(f3), .b(3'b110), .eq(comparator_14_eq));  // open: gt, lt
  Comparator #(.width(3)) comparator_15 (.a(f3), .b(3'b111), .eq(comparator_15_eq));  // open: gt, lt
  Comparator #(.width(7)) comparator_16 (.a({7{1'b0}}), .b(multiplexer_1_out), .eq(comparator_16_eq));  // open: gt, lt
  Comparator #(.width(7)) comparator_17 (.a(7'b0000001), .b(multiplexer_2_out), .eq(comparator_17_eq));  // open: gt, lt
  Comparator #(.width(7)) comparator_18 (.a(7'b0100000), .b(multiplexer_3_out), .eq(comparator_18_eq));  // open: gt, lt
  Comparator #(.width(7)) comparator_19 (.a({7{1'b0}}), .b(multiplexer_4_out), .eq(comparator_19_eq));  // open: gt, lt
  Comparator #(.width(7)) comparator_20 (.a(7'b0000001), .b(multiplexer_5_out), .eq(comparator_20_eq));  // open: gt, lt
  Comparator #(.width(7)) comparator_21 (.a({7{1'b0}}), .b(multiplexer_6_out), .eq(comparator_21_eq));  // open: gt, lt
  Comparator #(.width(7)) comparator_22 (.a({7{1'b0}}), .b(multiplexer_7_out), .eq(comparator_22_eq));  // open: gt, lt
  Comparator #(.width(7)) comparator_23 (.a(7'b0000001), .b(multiplexer_8_out), .eq(comparator_23_eq));  // open: gt, lt
  Comparator #(.width(7)) comparator_24 (.a({7{1'b0}}), .b(multiplexer_9_out), .eq(comparator_24_eq));  // open: gt, lt
  Comparator #(.width(7)) comparator_25 (.a({7{1'b0}}), .b(multiplexer_10_out), .eq(comparator_25_eq));  // open: gt, lt
  Comparator #(.width(7)) comparator_26 (
    .a(7'b0000001), .b(multiplexer_11_out), .eq(comparator_26_eq));  // open: gt, lt
  Comparator #(.width(7)) comparator_27 (.a({7{1'b0}}), .b(multiplexer_12_out), .eq(comparator_27_eq));  // open: gt, lt
  Multiplexer #(.width(4)) multiplexer_13 (
    .in1(4'b0010), .out(multiplexer_13_out), .sel(comparator_9_eq));  // open: in0, en
  Multiplexer #(.width(4)) multiplexer_14 (
    .in1(4'b0000), .out(multiplexer_13_out), .sel(comparator_10_eq));  // open: in0, en
  Multiplexer #(.width(4)) multiplexer_15 (
    .in1(4'b0110), .out(multiplexer_13_out), .sel(comparator_11_eq));  // open: in0, en
  Multiplexer #(.width(4)) multiplexer_16 (
    .in1(4'b0101), .out(multiplexer_13_out), .sel(comparator_12_eq));  // open: in0, en
  Multiplexer #(.width(4)) multiplexer_17 (
    .in1(4'b0001), .out(multiplexer_13_out), .sel(comparator_13_eq));  // open: in0, en
  Multiplexer #(.width(4)) multiplexer_18 (
    .in1(4'b0100), .out(multiplexer_13_out), .sel(comparator_14_eq));  // open: in0, en
  Multiplexer #(.width(4)) multiplexer_19 (
    .in1(4'b0011), .out(multiplexer_13_out), .sel(comparator_15_eq));  // open: in0, en
  Multiplexer #(.width(4)) multiplexer_20 (
    .in1(4'b0010), .out(multiplexer_20_out), .sel(comparator_16_eq));  // open: in0, en
  Multiplexer #(.width(4)) multiplexer_21 (
    .in1(4'b0111), .out(multiplexer_20_out), .sel(comparator_17_eq));  // open: in0, en
  Multiplexer #(.width(4)) multiplexer_22 (
    .in1(4'b1011), .out(multiplexer_20_out), .sel(comparator_18_eq));  // open: in0, en
  Multiplexer #(.width(4)) multiplexer_23 (
    .in1(4'b0000), .out(multiplexer_20_out), .sel(comparator_19_eq));  // open: in0, en
  Multiplexer #(.width(4)) multiplexer_24 (
    .in1(4'b1000), .out(multiplexer_20_out), .sel(comparator_20_eq));  // open: in0, en
  Multiplexer #(.width(4)) multiplexer_25 (
    .in1(4'b0110), .out(multiplexer_20_out), .sel(comparator_21_eq));  // open: in0, en
  Multiplexer #(.width(4)) multiplexer_26 (
    .in1(4'b0101), .out(multiplexer_20_out), .sel(comparator_22_eq));  // open: in0, en
  Multiplexer #(.width(4)) multiplexer_27 (
    .in1(4'b1001), .out(multiplexer_20_out), .sel(comparator_23_eq));  // open: in0, en
  Multiplexer #(.width(4)) multiplexer_28 (
    .in1(4'b0001), .out(multiplexer_20_out), .sel(comparator_24_eq));  // open: in0, en
  Multiplexer #(.width(4)) multiplexer_29 (
    .in1(4'b0100), .out(multiplexer_20_out), .sel(comparator_25_eq));  // open: in0, en
  Multiplexer #(.width(4)) multiplexer_30 (
    .in1(4'b1010), .out(multiplexer_20_out), .sel(comparator_26_eq));  // open: in0, en
  Multiplexer #(.width(4)) multiplexer_31 (
    .in1(4'b0011), .out(multiplexer_20_out), .sel(comparator_27_eq));  // open: in0, en
  Multiplexer #(.select(4), .width(4)) multiplexer_32 (
    .in0(multiplexer_20_out), .in1(multiplexer_13_out), .in2(4'b0010), .in3(4'b0010), .in4(4'b0010),
    .in5(4'b1111), .in6(4'b0010), .in7(4'b0010), .in8(4'b0010), .out(alida), .sel(seleccc));  // open: in9, in10, in11, in12, in13, in14, in15, en
endmodule

module br_compaator (
  input  [31:0] in_1,
  input  [31:0] in_2,
  input  [2:0] in_3,
  output out_4
);

  wire comparator_1_lt, comparator_2_eq, comparator_2_lt, multiplexer_1_out, multiplexer_2_out, not_1_out;

  Comparator #(.width(32)) comparator_1 (.a(in_2), .b(in_1), .lt(comparator_1_lt));  // open: gt, eq
  Comparator #(.width(32)) comparator_2 (.a(in_2), .b(in_1), .eq(comparator_2_eq), .lt(comparator_2_lt));  // open: gt
  Multiplexer multiplexer_1 (
    .in0(comparator_2_lt), .in1(comparator_1_lt), .out(multiplexer_1_out), .sel(in_3[1]));  // open: en
  Multiplexer multiplexer_2 (
    .in0(comparator_2_eq), .in1(multiplexer_1_out), .out(multiplexer_2_out), .sel(in_3[2]));  // open: en
  Multiplexer multiplexer_3 (.in0(multiplexer_2_out), .in1(not_1_out), .out(out_4), .sel(in_3[0]));  // open: en
  not not_1 (not_1_out, multiplexer_2_out);

  // Other names for the same wires on the sheet: A[31:0] = in_2; B[31:0] = in_1; f3[2:0] = in_3
endmodule
