// Logisim project regfile.circ as structural Verilog: 1 circuit, main circuit RegFile
module RegFile (
  input  [4:0] RD,
  input  [4:0] RS1,
  input  [4:0] RS2,
  input  [31:0] W,
  input  WE,
  input  Clk,
  output [31:0] s0,
  output [31:0] s1,
  output [31:0] t0,
  output [31:0] t1,
  output [31:0] a0,
  output [31:0] ra,
  output [31:0] sp,
  output [31:0] R1,
  output [31:0] R2
);

  wire and_1_out, and_2_out, and_3_out, and_4_out, and_5_out, and_6_out, and_7_out, and_8_out,
       decoder_1_out0, decoder_1_out1, decoder_1_out2, decoder_1_out5, decoder_1_out6, decoder_1_out8,
       decoder_1_out9, decoder_1_out10, decoder_1_out11;
  wire [31:0] a1_q, Zero_q;

  Decoder #(.select(5), .enable("false")) decoder_1 (
    .out0(decoder_1_out0), .out1(decoder_1_out1), .out2(decoder_1_out2), .out5(decoder_1_out5),
    .out6(decoder_1_out6), .out8(decoder_1_out8), .out9(decoder_1_out9), .out10(decoder_1_out10),
    .out11(decoder_1_out11), .sel(RD));  // open: out3, out4, out7, out12, out13, out14, out15, out16, out17, out18, out19, out20, out21, out22, out23, out24, out25, out26, out27, out28, out29, out30, out31
  and and_1 (and_1_out, WE, decoder_1_out1);
  and and_2 (and_2_out, WE, decoder_1_out2);
  and and_3 (and_3_out, WE, decoder_1_out5);
  and and_4 (and_4_out, WE, decoder_1_out6);
  and and_5 (and_5_out, WE, decoder_1_out8);
  and and_6 (and_6_out, WE, decoder_1_out9);
  and and_7 (and_7_out, WE, decoder_1_out10);
  and and_8 (and_8_out, WE, decoder_1_out11);
  Register #(.width(32)) Zero (.D({32{1'b0}}), .en(decoder_1_out0), .Q(Zero_q), .clk(Clk));  // open: clr
  Register #(.width(32)) u_ra (.D(W), .en(and_1_out), .Q(ra), .clk(Clk));  // open: clr
  Register #(.width(32)) u_sp (.D(W), .en(and_2_out), .Q(sp), .clk(Clk));  // open: clr
  Register #(.width(32)) u_t0 (.D(W), .en(and_3_out), .Q(t0), .clk(Clk));  // open: clr
  Register #(.width(32)) u_t1 (.D(W), .en(and_4_out), .Q(t1), .clk(Clk));  // open: clr
  Register #(.width(32)) u_s0 (.D(W), .en(and_5_out), .Q(s0), .clk(Clk));  // open: clr
  Register #(.width(32)) u_s1 (.D(W), .en(and_6_out), .Q(s1), .clk(Clk));  // open: clr
  Register #(.width(32)) u_a0 (.D(W), .en(and_7_out), .Q(a0), .clk(Clk));  // open: clr
  Register #(.width(32)) a1 (.D(W), .en(and_8_out), .Q(a1_q), .clk(Clk));  // open: clr
  Multiplexer #(.select(5), .width(32), .enable("false")) multiplexer_1 (
    .in0(Zero_q), .in1(ra), .in2(sp), .in5(t0), .in6(t1), .in8(s0), .in9(s1), .in10(a0), .in11(a1_q),
    .out(R1), .sel(RS1));  // open: in3, in4, in7, in12, in13, in14, in15, in16, in17, in18, in19, in20, in21, in22, in23, in24, in25, in26, in27, in28, in29, in30, in31
  Multiplexer #(.select(5), .width(32), .enable("false")) multiplexer_2 (
    .in0(Zero_q), .in1(ra), .in2(sp), .in5(t0), .in6(t1), .in8(s0), .in9(s1), .in10(a0), .in11(a1_q),
    .out(R2), .sel(RS2));  // open: in3, in4, in7, in12, in13, in14, in15, in16, in17, in18, in19, in20, in21, in22, in23, in24, in25, in26, in27, in28, in29, in30, in31

  // Notes on the sheet:
  //   Write Register
  //   Read Register 1
  //   Read Register 2
  //   Write Data
  //   Write Enable
  //   Clock
  //   NOTE
  //   Please do not modify/replace/move/change/delete/etc input and output pins
  //   These are debug/test outputs from your circuit
  //   Read Data 1
  //   Read Data 2
endmodule
